# Fritzing sketch avocado_temp_and_moisture (saved by Fritzing 0.9.2b)
breadboards: 1

parts:
  Part1 = Arduino Uno (Rev3)
  PART1 = SparkFun Soil Moisture Sensor [part_number=SEN-13322]
  R1 = Resistor [tolerance=±5% resistance=220 package=THT]
  R2 = Resistor [tolerance=±5% resistance=220 package=THT]
  R3 = Resistor [tolerance=±5% resistance=220 package=THT]
  LED1 = LED - 5mm [color="Green (565nm)" package="5 mm [THT]"]
  LED2 = LED - 5mm [color="Red (633nm)" package="5 mm [THT]"]
  LED3 = LED - 5mm [color="Yellow (595nm)" package="5 mm [THT]"]
  T2 = TMP36 Temperature Sensor [package="TO92 [THT]"]

nets:
  N1: Part1.A0, PART1.SIG
  N2: Part1.A1, T2.Vout
  N3: Part1.D8, R3.Pin_0
  N4: Part1.D9_PWM, R2.Pin_0
  N5: Part1.D10_PWM/SS, R1.Pin_0
  5V: Part1.5V, PART1.VCC, T2.+Vs
  GND: Part1.GND, PART1.GND, LED1.cathode, LED2.cathode, LED3.cathode, T2.GND
  N6: R1.Pin_1, LED1.anode
  N7: R2.Pin_1, LED3.anode
  N8: R3.Pin_1, LED2.anode

custom parts:
  SparkFun Soil Moisture Sensor: The SparkFun Soil Moisture Sensor is a simple breakout for measuring the moisture in soil and similar materials.

// code stored in the sketch: avocado_temp_and_moisture.ino
/*
 * environmental sensors for a potted avocado plant
 * soil moisture sensor readout controls 3 LEDs
 * temperature and soil moisture values are written to serial port
 */

const int SOIL_PIN = A0;
const int TEMP_PIN = A1;
const int GREEN = 8;
const int YELLOW = 9;
const int RED = 10;
float soil, temp;

void setup() {
  pinMode(SOIL_PIN, INPUT);
  pinMode(TEMP_PIN, INPUT);
  pinMode(GREEN, OUTPUT);
  pinMode(YELLOW, OUTPUT);
  pinMode(RED, OUTPUT);
  Serial.begin(9600);
}

void loop() {
  soil = getMoisturePercentageFrom(SOIL_PIN);
  temp = getTempFrom(TEMP_PIN);
  Serial.print("soil moisture ");
  Serial.print(soil);
  Serial.print("%, air temp ");
  Serial.print(temp);
  Serial.println("C.");
  
  if (soil >= 70) {
    digitalWrite(GREEN, HIGH);
    digitalWrite(YELLOW, HIGH);
    digitalWrite(RED, HIGH);
  } else if (soil >= 30) {
    digitalWrite(GREEN, LOW);
    digitalWrite(YELLOW, HIGH);
    digitalWrite(RED, HIGH);
  } else {
    digitalWrite(GREEN, LOW);
    digitalWrite(YELLOW, LOW);
    digitalWrite(RED, HIGH);
  }
  delay(1000);
}

float getTempFrom(int pin) {
  float tempReadout = analogRead(pin) * 0.004882814;
  return (tempReadout - 0.5) * 100.0;
}

float getMoisturePercentageFrom(int pin) {
  float soilReadout = analogRead(pin);
  return soilReadout/800.0 * 100.0;
}
